# Fritzing sketch Arduino-as-ISP-StatusLEDs (saved by Fritzing 0.9.2b)
breadboards: 1

parts:
  Parte1 = Arduino Uno (Rev3) - ICSP
  U1 = attiny85 [package=dip]
  C1 = Capacitor Polarized [package=cpol-radial-10uf-25v]
  R1 = Resistor [tolerance=±5% resistance=220 package="0603 [SMD]"]
  R2 = Resistor [tolerance=±5% resistance=220 package="0603 [SMD]"]
  R3 = Resistor [tolerance=±5% resistance=220 package="0603 [SMD]"]
  LED1 = LED - 5mm [color="Yellow (592nm)" package="5 mm [THT]"]
  LED2 = LED - 5mm [color="Red (633nm)" package="5 mm [THT]"]
  LED3 = LED - 5mm [color="Green (560nm)" package="5 mm [THT]"]

nets:
  N1: Parte1.D8, LED2.anode
  N2: Parte1.D9_PWM, LED1.anode
  N3: Parte1.D10_PWM/SS, U1.Pin_1
  N4: Parte1.D11_PWM/MOSI, U1.Pin_5
  N5: Parte1.D12/MISO, U1.Pin_6
  N6: Parte1.D13/SCK, U1.Pin_7
  N7: Parte1.D7, LED3.anode
  N8: Parte1.RESET, C1.-
  N9: Parte1.5V, U1.Pin_8
  N10: Parte1.GND, U1.Pin_4, C1.+, R1.Pin_0, R2.Pin_0
  N11: R1.Pin_1, LED1.cathode
  N12: R2.Pin_1, LED2.cathode
  N13: R3.Pin_1, LED3.cathode
