# Fritzing sketch Arduino-as-ISP (saved by Fritzing 0.9.2b)
breadboards: 1

parts:
  Parte1 = Arduino Uno (Rev3) - ICSP
  U1 = attiny85 [package=dip]
  C1 = Capacitor Polarized [package=cpol-radial-10uf-25v]

nets:
  N1: Parte1.D10_PWM/SS, U1.Pin_1
  N2: Parte1.D11_PWM/MOSI, U1.Pin_5
  N3: Parte1.D12/MISO, U1.Pin_6
  N4: Parte1.D13/SCK, U1.Pin_7
  N5: Parte1.RESET, C1.-
  N6: Parte1.5V, U1.Pin_8
  N7: Parte1.GND, U1.Pin_4, C1.+
